// Logisim project Project2.circ as structural Verilog: 13 circuits, main circuit MIPS32
module MIPS32 (
);

  wire clock_1_out, ctrlidex_1_com, ctrlidex_1_imm, ctrlidex_1_lui, ctrlidex_1_mov, ctrlidex_1_su,
       forward_1_exa, forward_1_exb, forward_1_mema, forward_1_memb, registerfile_1_p3;
  wire [3:0] ctrlidex_1_alu;
  wire [4:0] ctrlexmem_1_dest, decode_1_ra, decode_1_rb, decode_1_shamt, idex_1_sa, registerfile_1_p4;
  wire [31:0] bit_extender_1_out, compare_1_o, ctrlexmem_1_q, ctrlidex_1_ctrl, D_q, idex_1_qa, idex_1_qb,
       idex_1_qimm, incrementer4_1_out_2, lui_1_d, mips_alu_1_p5, mipsprogramrom_1_p2, mov_1_q,
       multiplexer_1_out, multiplexer_2_out, multiplexer_3_out, multiplexer_4_out, multiplexer_5_out,
       multiplexer_6_out, multiplexer_7_out, multiplexer_8_out, pc_1_o, register_1_q, registerfile_1_p1,
       registerfile_1_p7, registerfile_1_p8;

  PC pc_1 (.I(incrementer4_1_out_2), .Clk(clock_1_out), .O(pc_1_o));
  Incrementer4 incrementer4_1 (.in_1(pc_1_o), .out_2(incrementer4_1_out_2));
  // Probe on incrementer4_1_out_2
  // MIPSProgramROM mipsprogramrom_1: pin names not known; wires that end beside it: pc_1_o, mipsprogramrom_1_p2
  Register #(.width(32)) register_1 (.D(mipsprogramrom_1_p2), .clk(clock_1_out), .Q(register_1_q));  // open: en, clr
  Clock clock_1 (.out(clock_1_out));
  decode decode_1 (.I(register_1_q), .Shamt(decode_1_shamt), .rB(decode_1_rb), .rA(decode_1_ra));
  // RegisterFile #(.trigger("falling")) registerfile_1: pin names not known; wires that end beside it: registerfile_1_p1, clock_1_out, registerfile_1_p3, registerfile_1_p4, decode_1_ra, decode_1_rb, registerfile_1_p7, registerfile_1_p8
  assign bit_extender_1_out = {{16{register_1_q[15]}}, register_1_q[15:0]};  // Bit_Extender bit_extender_1
  IDEX idex_1 (
    .C(clock_1_out), .DA(registerfile_1_p7), .DB(registerfile_1_p8), .DIMM(bit_extender_1_out),
    .Shamt(decode_1_shamt), .QA(idex_1_qa), .QB(idex_1_qb), .QIMM(idex_1_qimm), .Sa(idex_1_sa));
  Forward forward_1 (
    .IDEXrs(decode_1_ra), .ExMemRd(ctrlexmem_1_dest), .MemWbRd(registerfile_1_p4), .IDEXrt(decode_1_rb),
    .Clk(clock_1_out), .ExA(forward_1_exa), .MemA(forward_1_mema), .MemB(forward_1_memb), .ExB(forward_1_exb));
  CtrlIDEX ctrlidex_1 (
    .D(register_1_q), .C(clock_1_out), .IMM(ctrlidex_1_imm), .Ctrl(ctrlidex_1_ctrl), .LUI(ctrlidex_1_lui),
    .Com(ctrlidex_1_com), .SU(ctrlidex_1_su), .ALU(ctrlidex_1_alu), .MOV(ctrlidex_1_mov));
  Multiplexer #(.width(32), .enable("false")) multiplexer_1 (
    .in0(idex_1_qa), .in1(registerfile_1_p1), .out(multiplexer_1_out), .sel(forward_1_mema));
  Multiplexer #(.width(32), .enable("false")) multiplexer_2 (
    .in0(multiplexer_1_out), .in1(D_q), .out(multiplexer_2_out), .sel(forward_1_exa));
  Multiplexer #(.width(32), .enable("false")) multiplexer_3 (
    .in0(idex_1_qb), .in1(idex_1_qimm), .out(multiplexer_3_out), .sel(ctrlidex_1_imm));
  Multiplexer #(.width(32), .enable("false")) multiplexer_4 (
    .in0(multiplexer_3_out), .in1(registerfile_1_p1), .out(multiplexer_4_out), .sel(forward_1_memb));
  Multiplexer #(.width(32), .enable("false")) multiplexer_5 (
    .in0(multiplexer_4_out), .in1(D_q), .out(multiplexer_5_out), .sel(forward_1_exb));
  // Mips_ALU mips_alu_1: pin names not known; wires that end beside it: multiplexer_2_out, multiplexer_5_out, ctrlidex_1_alu, idex_1_sa, mips_alu_1_p5
  compare compare_1 (.A(multiplexer_2_out), .B(multiplexer_5_out), .SU(ctrlidex_1_su), .O(compare_1_o));
  LUI lui_1 (.CTRL(ctrlidex_1_ctrl), .D(lui_1_d));
  Multiplexer #(.width(32), .enable("false")) multiplexer_6 (
    .in0(mips_alu_1_p5), .in1(multiplexer_2_out), .out(multiplexer_6_out), .sel(ctrlidex_1_mov));
  Multiplexer #(.width(32), .enable("false")) multiplexer_7 (
    .in0(multiplexer_6_out), .in1(compare_1_o), .out(multiplexer_7_out), .sel(ctrlidex_1_com));
  Multiplexer #(.width(32), .enable("false")) multiplexer_8 (
    .in0(multiplexer_7_out), .in1(lui_1_d), .out(multiplexer_8_out), .sel(ctrlidex_1_lui));
  MOV mov_1 (.B(multiplexer_5_out), .D(ctrlidex_1_ctrl), .Q(mov_1_q));
  Register #(.width(32)) D (.D(multiplexer_8_out), .clk(clock_1_out), .Q(D_q));  // open: en, clr
  CtrlEXMEM ctrlexmem_1 (.D(mov_1_q), .C(clock_1_out), .Q(ctrlexmem_1_q), .dest(ctrlexmem_1_dest));
  Register #(.width(32)) D_2 (.D(D_q), .clk(clock_1_out), .Q(registerfile_1_p1));  // open: en, clr
  CtrlMEMWB ctrlmemwb_1 (.D(ctrlexmem_1_q), .C(clock_1_out), .dest(registerfile_1_p4), .WE(registerfile_1_p3));

  // Notes on the sheet:
  //   contents of mipsprogramrom_1 (hex, n*v repeats v):
  //   ADDIU $t1, $0, 5 ADDIU $t2, $0, 10 BNE $t6, $0, 0 #Should do nothing, used to make sure no
  //   #forwarded add instructions work SLL $t0, $t0, 0# Another delay instruction SLL $t5, $t2, 2 #Testing
  //   SLL, value in $t5 should be 40 (0x28) SRL $t0, $t5, 1 #Testing Forwarding and SRL, value in $t0
  //   should be 20 (0x14) ADDU $t3, $t1, $t2 ADDU $t4, $t3, $0 #Testing M/X Forwarding, value in $t4
  //   should be 15 (0xf) ADDU $t0, $t4, $t3 #Testing W/x Forwarding, value in $t0 should be 30 (0x1e) AND
  //   $t6, $t5, $t2 #Value in $t6 should be 8 (0x8) MOVN $t7, $t6, $t2 #Value in $t7 should be 8 because
  //   $t6 is not 0
endmodule

module Incrementer4 (
  input  [31:0] in_1,
  output [31:0] out_2
);

  // Incrementer #(.width(30)) incrementer_1: pin names not known; wires that end beside it: in_1[31:2], out_2[31:2]

  assign out_2[1:0] = in_1[1:0];
endmodule

module PC (
  input  [31:0] I,
  input  Clk,
  output [31:0] O
);

  Register #(.width(32)) register_1 (.D(I), .clk(Clk), .Q(O));  // open: en, clr
endmodule

module IDEX (
  input  C,
  input  [31:0] DA,
  input  [31:0] DB,
  input  [31:0] DIMM,
  input  [4:0] Shamt,
  output [31:0] QA,
  output [31:0] QB,
  output [31:0] QIMM,
  output [4:0] Sa
);

  Register #(.width(32)) register_1 (.D(DA), .clk(C), .Q(QA));  // open: en, clr
  Register #(.width(5)) register_2 (.D(Shamt), .clk(C), .Q(Sa));  // open: en, clr
  Register #(.width(32)) register_3 (.D(DB), .clk(C), .Q(QB));  // open: en, clr
  Register #(.width(32)) register_4 (.D(DIMM), .clk(C), .Q(QIMM));  // open: en, clr
endmodule

module CtrlIDEX (
  input  [31:0] D,
  input  C,
  output IMM,
  output [31:0] Ctrl,
  output LUI,
  output Com,
  output SU,
  output [3:0] ALU,
  output MOV
);

  wire and_1_out, and_3_out, and_4_out, and_5_out, and_6_out, and_7_out, and_8_out, and_9_out, and_10_out,
       and_11_out, and_12_out, and_13_out, and_14_out, and_17_out, not_1_out, not_2_out, not_3_out,
       not_4_out, not_5_out, not_6_out, not_7_out, not_8_out, not_9_out, not_10_out, not_11_out, not_12_out,
       not_13_out, not_14_out, not_15_out, not_16_out, not_17_out, not_18_out, not_19_out, not_20_out;
  wire [3:0] or_4_out;

  Register #(.width(32)) register_1 (.D(D), .clk(C), .Q(Ctrl));  // open: en, clr
  not not_1 (not_1_out, Ctrl[31]);
  not not_2 (not_2_out, Ctrl[30]);
  not not_3 (not_3_out, Ctrl[1]);
  not not_4 (not_4_out, Ctrl[3]);
  and and_1 (and_1_out, Ctrl[5], Ctrl[0]);
  not not_5 (not_5_out, Ctrl[5]);
  not not_6 (not_6_out, Ctrl[3]);
  not not_7 (not_7_out, Ctrl[31]);
  not not_8 (not_8_out, Ctrl[30]);
  not not_9 (not_9_out, Ctrl[28]);
  not not_10 (not_10_out, Ctrl[31]);
  not not_11 (not_11_out, Ctrl[30]);
  not not_12 (not_12_out, Ctrl[28]);
  not not_13 (not_13_out, Ctrl[31]);
  not not_14 (not_14_out, Ctrl[30]);
  not not_15 (not_15_out, Ctrl[27]);
  not not_16 (not_16_out, Ctrl[31]);
  not not_17 (not_17_out, Ctrl[30]);
  not not_18 (not_18_out, Ctrl[26]);
  and and_2 (LUI, not_1_out, not_2_out, Ctrl[29], Ctrl[28], Ctrl[27], Ctrl[26]);
  not not_19 (not_19_out, Ctrl[30]);
  not not_20 (not_20_out, Ctrl[28]);
  and and_3 (and_3_out, Ctrl[3], not_3_out);
  and and_4 (and_4_out, Ctrl[3], Ctrl[2]);
  and and_5 (and_5_out, Ctrl[5], Ctrl[2]);
  and and_6 (and_6_out, not_4_out, Ctrl[1]);
  and and_7 (and_7_out, Ctrl[3], Ctrl[2]);
  or or_1 (or_4_out[1], Ctrl[3], and_1_out);
  and and_8 (and_8_out, not_5_out, not_6_out, Ctrl[0]);
  and and_9 (and_9_out, Ctrl[3], Ctrl[2]);
  and and_10 (and_10_out, ~Ctrl[5], ~Ctrl[4], Ctrl[3], ~Ctrl[2], Ctrl[1]);  // AND_Gate
  and and_11 (and_11_out, not_7_out, not_8_out, Ctrl[29], not_9_out, Ctrl[26]);
  and and_12 (and_12_out, not_10_out, not_11_out, Ctrl[29], not_12_out, Ctrl[27]);
  and and_13 (and_13_out, not_13_out, not_14_out, Ctrl[29], Ctrl[28], not_15_out);
  and and_14 (and_14_out, not_16_out, not_17_out, Ctrl[29], Ctrl[28], not_18_out);
  and and_15 (Com, not_19_out, Ctrl[29], not_20_out, Ctrl[27]);
  and and_16 (SU, ~Ctrl[30], Ctrl[29], ~Ctrl[28], Ctrl[27], Ctrl[26]);  // AND_Gate
  or or_2 (or_4_out[3], and_3_out, and_4_out, and_5_out);
  or or_3 (or_4_out[2], and_6_out, and_7_out);
  or or_4 (or_4_out[0], and_8_out, and_9_out);
  and and_17 (and_17_out, ~Ctrl[31], ~Ctrl[30], ~Ctrl[29], ~Ctrl[27], ~Ctrl[26], ~Ctrl[28]);  // AND_Gate
  or or_5 (IMM, and_11_out, and_12_out, and_13_out, and_14_out);
  and and_18 (MOV, and_10_out, and_17_out);
  Multiplexer #(.width(4), .enable("false")) multiplexer_1 (
    .in0(or_4_out), .in1({Ctrl[28:26], Ctrl[31]}), .out(ALU), .sel(IMM));
endmodule

module CtrlMEMWB (
  input  [31:0] D,
  input  C,
  output [4:0] dest,
  output WE
);

  wire and_1_out, and_2_out, and_3_out, and_4_out, and_5_out, and_6_out, and_7_out, and_8_out, and_9_out,
       and_10_out, not_1_out, not_2_out, not_3_out, not_4_out, not_5_out, not_6_out, not_7_out, not_8_out,
       not_9_out, not_10_out, not_11_out, not_12_out, not_13_out, not_14_out, not_15_out, not_16_out,
       not_17_out, not_18_out, not_19_out, not_20_out, not_21_out, not_22_out, not_23_out, not_24_out,
       not_25_out, not_26_out, not_27_out, or_1_out, or_2_out;
  wire [31:0] register_1_q;

  Register #(.width(32)) register_1 (.D(D), .clk(C), .Q(register_1_q));  // open: en, clr
  and and_1 (and_1_out, ~register_1_q[31], ~register_1_q[30], register_1_q[29], register_1_q[27], register_1_q[26], register_1_q[28]);  // AND_Gate
  not not_1 (not_1_out, register_1_q[5]);
  not not_2 (not_2_out, register_1_q[4]);
  not not_3 (not_3_out, register_1_q[3]);
  not not_4 (not_4_out, register_1_q[0]);
  not not_5 (not_5_out, register_1_q[5]);
  not not_6 (not_6_out, register_1_q[4]);
  not not_7 (not_7_out, register_1_q[3]);
  not not_8 (not_8_out, register_1_q[5]);
  not not_9 (not_9_out, register_1_q[4]);
  not not_10 (not_10_out, register_1_q[2]);
  not not_11 (not_11_out, register_1_q[4]);
  not not_12 (not_12_out, register_1_q[3]);
  not not_13 (not_13_out, register_1_q[0]);
  not not_14 (not_14_out, register_1_q[4]);
  not not_15 (not_15_out, register_1_q[3]);
  not not_16 (not_16_out, register_1_q[31]);
  not not_17 (not_17_out, register_1_q[30]);
  not not_18 (not_18_out, register_1_q[28]);
  not not_19 (not_19_out, register_1_q[31]);
  not not_20 (not_20_out, register_1_q[30]);
  not not_21 (not_21_out, register_1_q[28]);
  not not_22 (not_22_out, register_1_q[31]);
  not not_23 (not_23_out, register_1_q[30]);
  not not_24 (not_24_out, register_1_q[27]);
  not not_25 (not_25_out, register_1_q[31]);
  not not_26 (not_26_out, register_1_q[30]);
  not not_27 (not_27_out, register_1_q[26]);
  and and_2 (and_2_out, not_1_out, not_2_out, not_3_out, not_4_out);
  and and_3 (and_3_out, not_5_out, not_6_out, not_7_out, register_1_q[1]);
  and and_4 (and_4_out, not_8_out, not_9_out, not_10_out, register_1_q[1]);
  and and_5 (and_5_out, not_11_out, not_12_out, register_1_q[2], not_13_out);
  and and_6 (and_6_out, register_1_q[5], not_14_out, not_15_out, register_1_q[0]);
  and and_7 (and_7_out, not_16_out, not_17_out, register_1_q[29], not_18_out, register_1_q[26]);
  and and_8 (and_8_out, not_19_out, not_20_out, register_1_q[29], not_21_out, register_1_q[27]);
  and and_9 (and_9_out, not_22_out, not_23_out, register_1_q[29], register_1_q[28], not_24_out);
  and and_10 (and_10_out, not_25_out, not_26_out, register_1_q[29], register_1_q[28], not_27_out);
  or or_1 (or_1_out, and_2_out, and_3_out, and_4_out, and_5_out, and_6_out);
  Multiplexer #(.width(5), .enable("false")) multiplexer_1 (
    .in0(register_1_q[15:11]), .in1(register_1_q[20:16]), .out(dest), .sel(or_2_out));
  or or_2 (or_2_out, and_7_out, and_8_out, and_1_out, and_9_out, and_10_out);
  or or_3 (WE, or_2_out, or_1_out);

  // Notes on the sheet:
  //   dest.
endmodule

module compare (
  input  [31:0] A,
  input  [31:0] B,
  input  SU,
  output [31:0] O
);

  wire comparator_1_eq, comparator_2_eq, multiplexer_1_out;

  Comparator #(.width(32)) comparator_1 (.a(A), .b(B), .eq(comparator_1_eq));  // open: gt, lt
  Comparator #(.width(32), .mode("unsigned")) comparator_2 (.a(A), .b(B), .eq(comparator_2_eq));  // open: gt, lt
  Multiplexer #(.enable("false")) multiplexer_1 (
    .in0(comparator_1_eq), .in1(comparator_2_eq), .out(multiplexer_1_out), .sel(SU));
  assign O = {{31{1'b0}}, multiplexer_1_out};  // Bit_Extender bit_extender_1

  // Notes on the sheet:
  //   signed
  //   unsigned
endmodule

module decode (
  input  [31:0] I,
  output [4:0] Shamt,
  output [4:0] rB,
  output [4:0] rA
);


  assign rA = I[25:21];
  assign rB = I[20:16];
  assign Shamt = I[10:6];
endmodule

module test (
  input  I5,
  input  I4,
  input  I3,
  input  I2,
  input  I1,
  input  I0,
  output O3,
  output O2,
  output O1,
  output O0
);


  assign O0 = 1'b0;
  assign O1 = I0;
  assign O2 = I1;
  assign O3 = I2;
endmodule

module CtrlEXMEM (
  input  [31:0] D,
  input  C,
  output [31:0] Q,
  output [4:0] dest
);

  wire and_1_out, and_2_out, and_3_out, and_4_out, and_5_out, not_1_out, not_2_out, not_3_out, not_4_out,
       not_5_out, not_6_out, not_7_out, not_8_out, not_9_out, not_10_out, not_11_out, not_12_out, or_1_out;

  Register #(.width(32)) register_1 (.D(D), .clk(C), .Q(Q));  // open: en, clr
  and and_1 (and_1_out, ~Q[31], ~Q[30], Q[29], Q[27], Q[26], Q[28]);  // AND_Gate
  not not_1 (not_1_out, Q[31]);
  not not_2 (not_2_out, Q[30]);
  not not_3 (not_3_out, Q[28]);
  not not_4 (not_4_out, Q[31]);
  not not_5 (not_5_out, Q[30]);
  not not_6 (not_6_out, Q[28]);
  not not_7 (not_7_out, Q[31]);
  not not_8 (not_8_out, Q[30]);
  not not_9 (not_9_out, Q[27]);
  not not_10 (not_10_out, Q[31]);
  not not_11 (not_11_out, Q[30]);
  not not_12 (not_12_out, Q[26]);
  and and_2 (and_2_out, not_1_out, not_2_out, Q[29], not_3_out, Q[26]);
  and and_3 (and_3_out, not_4_out, not_5_out, Q[29], not_6_out, Q[27]);
  and and_4 (and_4_out, not_7_out, not_8_out, Q[29], Q[28], not_9_out);
  and and_5 (and_5_out, not_10_out, not_11_out, Q[29], Q[28], not_12_out);
  Multiplexer #(.width(5), .enable("false")) multiplexer_1 (.in0(Q[15:11]), .in1(Q[20:16]), .out(dest), .sel(or_1_out));
  or or_1 (or_1_out, and_2_out, and_3_out, and_1_out, and_4_out, and_5_out);

  // Notes on the sheet:
  //   dest.
endmodule

module Forward (
  input  [4:0] IDEXrs,
  input  [4:0] ExMemRd,
  input  [4:0] MemWbRd,
  input  [4:0] IDEXrt,
  input  Clk,
  output ExA,
  output MemA,
  output MemB,
  output ExB
);

  wire and_2_out, and_3_out, nor_1_out, nor_2_out, nor_3_out, nor_4_out, not_1_out, not_2_out, or_1_out,
       or_2_out;
  wire [4:0] register_1_q, register_2_q, xor_1_out, xor_2_out, xor_3_out, xor_4_out;

  Register #(.width(5)) register_1 (.D(IDEXrs), .clk(Clk), .Q(register_1_q));  // open: en, clr
  Register #(.width(5)) register_2 (.D(IDEXrt), .clk(Clk), .Q(register_2_q));  // open: en, clr
  assign xor_1_out = register_1_q ^ ExMemRd;  // XOR_Gate xor_1, 5 bits wide
  or or_1 (or_1_out, ExMemRd[0], ExMemRd[1], ExMemRd[2], ExMemRd[3], ExMemRd[4]);
  or or_2 (or_2_out, MemWbRd[0], MemWbRd[1], MemWbRd[2], MemWbRd[3], MemWbRd[4]);
  assign xor_2_out = register_1_q ^ MemWbRd;  // XOR_Gate xor_2, 5 bits wide
  assign xor_3_out = MemWbRd ^ register_2_q;  // XOR_Gate xor_3, 5 bits wide
  assign xor_4_out = register_2_q ^ ExMemRd;  // XOR_Gate xor_4, 5 bits wide
  nor nor_1 (nor_1_out, xor_1_out[0], xor_1_out[1], xor_1_out[2], xor_1_out[3], xor_1_out[4]);
  nor nor_2 (nor_2_out, xor_2_out[0], xor_2_out[1], xor_2_out[2], xor_2_out[3], xor_2_out[4]);
  nor nor_3 (nor_3_out, xor_3_out[0], xor_3_out[1], xor_3_out[2], xor_3_out[3], xor_3_out[4]);
  nor nor_4 (nor_4_out, xor_4_out[0], xor_4_out[1], xor_4_out[2], xor_4_out[3], xor_4_out[4]);
  and and_1 (ExA, nor_1_out, or_1_out);
  not not_1 (not_1_out, ExA);
  and and_2 (and_2_out, or_2_out, nor_2_out);
  and and_3 (and_3_out, or_2_out, nor_3_out);
  and and_4 (ExB, or_1_out, nor_4_out);
  not not_2 (not_2_out, ExB);
  and and_5 (MemA, not_1_out, and_2_out);
  and and_6 (MemB, and_3_out, not_2_out);
endmodule

module LUI (
  input  [31:0] CTRL,
  output [31:0] D
);

  wire not_1_out;

  not not_1 (not_1_out, CTRL[0]);
  and and_1 (D[15], not_1_out, CTRL[0]);

  assign {D[31:16], D[14:0]} = {CTRL[15:0], {15{D[15]}}};
endmodule

module MOV (
  input  [31:0] B,
  input  [31:0] D,
  output [31:0] Q
);

  wire and_1_out, and_2_out, N_out, or_1_out, Z_out;
  wire [31:0] multiplexer_1_out;

  or or_1 (or_1_out, B[0], B[1], B[2], B[3], B[4], B[5], B[6], B[7], B[8], B[9], B[10], B[11], B[12], B[13], B[14], B[15], B[17], B[18], B[19], B[20], B[21], B[22], B[23], B[24], B[25], B[26], B[27], B[28], B[29], B[30], B[31], B[16]);
  and N (N_out, ~D[5], ~D[4], D[3], ~D[2], D[1], D[0]);  // AND_Gate
  and Z (Z_out, ~D[5], ~D[4], D[3], ~D[2], D[1], ~D[0]);  // AND_Gate
  and and_1 (and_1_out, ~or_1_out, N_out);  // AND_Gate
  and and_2 (and_2_out, or_1_out, Z_out);
  Multiplexer #(.width(32), .enable("false")) multiplexer_1 (
    .in0(D), .in1({D[31:16], D[24:20], D[10:0]}), .out(multiplexer_1_out), .sel(and_1_out));
  Multiplexer #(.width(32), .enable("false")) multiplexer_2 (
    .in0(multiplexer_1_out), .in1({D[31:16], D[25:21], D[10:0]}), .out(Q), .sel(and_2_out));
endmodule
